# Fritzing sketch Schematic (saved by Fritzing 0.9.3b)
breadboards: 1

parts:
  M1 = DC Motor
  M2 = DC Motor
  Part1 = Arduino Uno (Rev3) - ICSP
  VCC1 = Battery block 9V  # not connected
  VCC2 = Battery
  Part2 = HC-SR04 Ultrasonic Rangemeter
  Part3 = Bluetooth HC-06
  VCC3 = Battery
  PART2 = Sound Detector
  PART3 = Sound Detector
  PART4 = Sound Detector
  S2 = H-Bridge with L298N
  J3 = Basic Servo

nets:
  N1: M1.pin_1, S2.M1-02
  N2: M1.pin_2, S2.M1-01
  N3: M2.pin_1, S2.M2-02, S2.ENB-5V
  N4: M2.pin_2, S2.M2-01
  N5: Part1.A0, Part2.Trig
  N6: Part1.A1, Part2.Echo
  GND: Part1.A2, Part1.GND, Part2.GND, Part3.GND, VCC3.-, PART2.GND, PART3.GND, PART4.GND, S2.GND, J3.gnd
  N7: Part1.A3, PART4.ENVELOPE
  N8: Part1.A4/SDA, PART3.ENVELOPE
  N9: Part1.A5/SCL, PART2.ENVELOPE
  VCC: Part1.5V, Part2.VCC, PART2.VCC, PART3.VCC, PART4.VCC
  N10: Part1.D10_PWM/SS, J3.pulse
  N11: Part1.D0/RX, Part3.TXD
  N12: Part1.D1/TX, Part3.RXD
  N13: Part1.D4, S2.IN4
  N14: Part1.D5_PWM, S2.IN3
  N15: Part1.D6_PWM, S2.IN2
  N16: Part1.D7, S2.IN1
  VCC_2: VCC2.+, Part3.VCC, S2.12V, J3.vcc

custom parts:
  Sound Detector: Electret microphone with multiple outputs. - First output is the actual audio - Second output is the amplitude envelope - Third output is a binary "sound present" indication - high while sound is present, low otherwise. Visit sparkfun.com for more documentations.
  H-Bridge with L298N: h-bridge
